# Fritzing sketch ecg_remoto (saved by Fritzing 0.9.3b)
circuit board: 8.46667cm x 5.64444cm
breadboards: 2

parts:
  LCD1 = 2.8" SPI TFT Module [part_number=MSP2807]
  U1 = ESP32-38PinWide [part_number=ESP32-38PinWide]
  IC1 = AD8232 HeartRate Monitor [part_number=SEN-12650 chip_label=IC package="DIP (Dual Inline) [THT]"]
  WeMos_D1_Mini1 = WeMos D1 Mini
  LED1 = LED - 5mm [color="White (6500K)" package="5 mm [THT]"]
  LED2 = LED - 5mm [color="Blue (430nm)" package="5 mm [THT]"]
  OLED_I2C1 = OLED 128x64 I2C Monochrome Display
  LED3 = LED - 5mm [color="Yellow (592nm)" package="5 mm [THT]"]
  LED4 = LED - 5mm [color="Red (633nm)" package="5 mm [THT]"]
  R2 = Resistor [tolerance=±5% resistance=330 package=THT]
  R3 = Resistor [tolerance=±5% resistance=330 package=THT]
  LED5 = LED - 5mm [color="Green (555nm)" package="5 mm [THT]"]
  R4 = Resistor [tolerance=±5% resistance=330 package=THT]
  R5 = Resistor [tolerance=±5% resistance=330 package=THT]
  R6 = Resistor [tolerance=±5% resistance=330 package=THT]

nets:
  N1: LCD1.pin1, LCD1.pin8, U1.3.3
  N2: LCD1.pin2, U1.GND, LED1.cathode, LED5.cathode
  N3: LCD1.pin3, U1.GPIO32
  N4: LCD1.pin4, U1.GPIO2
  N5: LCD1.pin5, U1.GPIO33
  N6: LCD1.pin6, LCD1.pin12, U1.GPIO13
  N7: LCD1.pin7, LCD1.pin10, U1.GPIO14
  N8: LCD1.pin9, LCD1.pin13, U1.GPIO12
  N9: LCD1.pin11, U1.GPIO27
  N10: LCD1.pin14, U1.GPIO26
  N11: U1.GPIO25, R4.Pin_1
  N12: U1.GPIO4, R3.Pin_1
  GND: IC1.GND, WeMos_D1_Mini1.G, OLED_I2C1.GND, R2.Pin_0, R5.Pin_0, R6.Pin_0
  3.3V: IC1.3.3v, WeMos_D1_Mini1.3V3, OLED_I2C1.VDD
  N13: IC1.OUTPUT, WeMos_D1_Mini1.A0
  N14: IC1.LO-, WeMos_D1_Mini1.D3
  N15: IC1.LO+, WeMos_D1_Mini1.D4
  N16: WeMos_D1_Mini1.D0, LED2.anode
  N17: WeMos_D1_Mini1.D1, OLED_I2C1.SCK
  N18: WeMos_D1_Mini1.D2, OLED_I2C1.SDA
  N19: WeMos_D1_Mini1.D5, LED3.anode
  N20: WeMos_D1_Mini1.D6, LED4.anode
  N21: LED1.anode, R3.Pin_0
  N22: LED2.cathode, R5.Pin_1
  N23: LED3.cathode, R2.Pin_1
  N24: LED4.cathode, R6.Pin_1
  N25: LED5.anode, R4.Pin_0

custom parts:
  2.8" SPI TFT Module: A generic 2.8 inch LCD TFT 320x240 display with touchscreen and SD card slot. Uses the ILI9341 controller, like the Adafruit displays of this size uses.
  ESP32-38PinWide: Generic 38-Pin ESP32 with wide format (only access to one side of pins on a breadboard) based on Stephen Lilley's HiLetgo ESP-WROOM-32 ESP32 ESP-32S Development Board.
  AD8232 HeartRate Monitor: A DIP stand-in part for whatever IC you want. With 10 pins on a 600mil dual inline package (DIP) footprint.
